# Fritzing sketch circuit (saved by Fritzing 0.9.4)
breadboards: 1

parts:
  Part1 = Arduino Nano (Rev3.0)
  MOTOR1 = 28BYJ-48 Stepper Motor
  IC1 = ULN2003A [package="SO16 [SMD]"]
  DHT1 = DHT22 Humidity and Temperature Sensor

nets:
  GND: Part1.GND, IC1.0V, DHT1.GND
  N1: Part1.D4, IC1.In_1
  N2: Part1.D5, IC1.In_2
  N3: Part1.D6, IC1.In_3
  N4: Part1.D7, IC1.In_4
  N5: Part1.D8, DHT1.DATA
  5V: Part1.5V, MOTOR1.RED, IC1.COM_-_Common, DHT1.VDD
  N6: MOTOR1.ORANGE, IC1.Out_4
  N7: MOTOR1.YELLOW, IC1.Out_3
  N8: MOTOR1.PINK, IC1.Out_2
  N9: MOTOR1.BLUE, IC1.Out_1
